# Fritzing sketch montagem_frdm (saved by Fritzing 0.9.4)
breadboards: 1

parts:
  FRDM-KL25Z1 = FRDM-KL25Z [part_number=FRDM-KL25Z]
  Componente1 = NRF24L01+ Breakout Board

nets:
  N1: FRDM-KL25Z1.D4_PTA4, Componente1.SCK
  N2: FRDM-KL25Z1.D8_PTA13, Componente1.IRQ
  N3: FRDM-KL25Z1.D9_PTD5_PWM, Componente1.CE
  N4: FRDM-KL25Z1.D10_PTD0_PWM, Componente1.CS
  N5: FRDM-KL25Z1.D11_PTD2_PWM, Componente1.MOSI
  N6: FRDM-KL25Z1.D12_PTD3, Componente1.MISO
  GND3: FRDM-KL25Z1.GND3, Componente1.GND
  N7: FRDM-KL25Z1.P3V3_2, Componente1.VCC

custom parts:
  FRDM-KL25Z: Freedom Board, based on basic pinout of Arduino Rev.3. Attention: the board is NOT 5V compatible.
