# Fritzing sketch montagem_frdm_nucleo (saved by Fritzing 0.9.4)
breadboards: 2

parts:
  FRDM-KL25Z1 = FRDM-KL25Z [part_number=FRDM-KL25Z]
  Componente1 = NRF24L01+ Breakout Board
  J1 = STM32 Nucleo boards [part_number=F411RE]
  Componente2 = NRF24L01+ Breakout Board

nets:
  N1: FRDM-KL25Z1.D4_PTA4, Componente1.SCK
  N2: FRDM-KL25Z1.D8_PTA13, Componente1.IRQ
  N3: FRDM-KL25Z1.D9_PTD5_PWM, Componente1.CE
  N4: FRDM-KL25Z1.D10_PTD0_PWM, Componente1.CS
  N5: FRDM-KL25Z1.D11_PTD2_PWM, Componente1.MOSI
  N6: FRDM-KL25Z1.D12_PTD3, Componente1.MISO
  GND3: FRDM-KL25Z1.GND3, Componente1.GND
  N7: FRDM-KL25Z1.P3V3_2, Componente1.VCC
  N8: J1.D8, Componente2.IRQ
  N9: J1.D9_PWM, Componente2.CE
  N10: J1.D10_PWM/SS, Componente2.CS
  N11: J1.D11_PWM/MOSI, Componente2.MOSI
  N12: J1.D12/MISO, Componente2.MISO
  N13: J1.D4, Componente2.SCK
  3V3: J1.3V3, Componente2.VCC
  GND: J1.GND, Componente2.GND

custom parts:
  FRDM-KL25Z: Freedom Board, based on basic pinout of Arduino Rev.3. Attention: the board is NOT 5V compatible.
